# Fritzing sketch Circuito_guante - v2 (saved by Fritzing 1.0.5)
perfboards: 1

parts:
  R1 = Basic Flex Resistor  # not connected
  R2 = Basic Flex Resistor  # not connected
  Componente1 = Analog Digital MUX Breakout
  Componente2 = ADS1115
  A1 = Esp32-c3 super mini
  U1 = POT [knob_status=50% power=0.5W package=pot_mammoth]
  U2 = POT [knob_status=50% power=0.5W package=pot_mammoth]
  U3 = POT [knob_status=50% power=0.5W package=pot_mammoth]
  U4 = POT [knob_status=50% power=0.5W package=pot_mammoth]
  U5 = POT [knob_status=50% power=0.5W package=pot_mammoth]
  R3 = Basic Flex Resistor  # not connected
  R4 = Basic Flex Resistor  # not connected
  R5 = Basic Flex Resistor  # not connected
  R6 = Resistor [tolerance=±5% resistance=220 package="0805 [SMD]"]
  R7 = Resistor [tolerance=±5% resistance=220 package="0805 [SMD]"]
  R8 = Resistor [tolerance=±5% resistance=220 package="0805 [SMD]"]
  R9 = Resistor [tolerance=±5% resistance=220 package="0805 [SMD]"]
  R10 = Resistor [tolerance=±5% resistance=220 package="0805 [SMD]"]
  U6 = POT [knob_status=50% power=0.5W package=pot_mammoth]  # not connected
  R11 = Basic Flex Resistor
  R12 = Basic Flex Resistor
  R13 = Resistor [tolerance=±5% resistance=220 package="0805 [SMD]"]
  R14 = Resistor [tolerance=±5% resistance=220 package="0805 [SMD]"]
  Componente3 = Analog Digital MUX Breakout
  R15 = Rotary Potentiometer (Small) [maximum_resistance=100kΩ knob_status=50% power=0.5W package=THT]
  R16 = Rotary Potentiometer (Small) [maximum_resistance=100kΩ knob_status=50% power=0.5W package=THT]
  R17 = Rotary Potentiometer (Small) [maximum_resistance=100kΩ knob_status=50% power=0.5W package=THT]
  R18 = Rotary Potentiometer (Small) [maximum_resistance=100kΩ knob_status=50% power=0.5W package=THT]  # not connected
  R19 = Rotary Potentiometer (Small) [maximum_resistance=100kΩ knob_status=50% power=0.5W package=THT]
  R20 = Rotary Potentiometer (Small) [maximum_resistance=100kΩ knob_status=50% power=0.5W package=THT]  # not connected
  R21 = Rotary Potentiometer (Small) [maximum_resistance=100kΩ knob_status=50% power=0.5W package=THT]  # not connected
  R22 = Rotary Potentiometer (Small) [maximum_resistance=100kΩ knob_status=50% power=0.5W package=THT]  # not connected
  R23 = Rotary Potentiometer (Small) [maximum_resistance=100kΩ knob_status=50% power=0.5W package=THT]  # not connected
  R24 = Rotary Potentiometer (Small) [maximum_resistance=100kΩ knob_status=50% power=0.5W package=THT]  # not connected
  C1 = Capacitor [package=cap-pth-small2]
  C2 = Capacitor [package=cap-pth-small2]  # not connected
  C3 = Capacitor [package=cap-pth-small2]  # not connected
  C4 = Capacitor [package=cap-pth-small2]  # not connected

nets:
  N1: Componente1.C1, R10.Pin_0
  N2: Componente1.C2, R8.Pin_0
  N3: Componente1.C3, R7.Pin_0
  N4: Componente1.C4, R6.Pin_0
  N5: Componente1.C7, U4.A
  N6: Componente1.C8, U1.A
  N7: Componente1.C9, U3.A
  N8: Componente1.C10, U2.A
  N9: Componente1.C11, U5.A
  N10: Componente1.EN, C1.1
  N11: Componente1.S0, A1.Pin_6
  N12: Componente1.S1, A1.Pin_11
  N13: Componente1.S2, A1.Pin_12
  N14: Componente1.SIG, Componente2.A0
  N15: Componente2.SDA, A1.Pin_4
  N16: Componente2.A1, Componente3.SIG
  N17: R9.Pin_0, Componente3.C0
  N18: R11.Pin_1, R13.Pin_0
  N19: R12.Pin_1, R14.Pin_0
  N20: Componente3.C1, R19.wiper
  N21: Componente3.C3, R16.wiper
  N22: Componente3.C4, R15.wiper
  N23: Componente3.C5, R17.wiper

notes:
  Circuito guante
  D1
  D2
  D3
  D4
  D5
  M1
  M2
  P0
  P1
  P2
  P3
  P4
  P5
  Ads1115
  CD74hc4067
  ESP32-S3 mini
  POTENCIOMETROS
  SENSORES FLEX DEDOS
  NOTA: P5 opcional (mov rotacional de muñeca)
  En caso de utilizarse se necesita otro multiplexor
  SENSORES FLEX MUÑECA
  SENSORES MOVIMIENTO DE ABDUCCION

custom parts:
  ADS1115: ADC ADS1115
  Esp32-c3 super mini: ESP32-C3 Development Board ESP32 SuperMini Development Board ESP32 Development Board WiFi Bluetooth.
