# Fritzing sketch Circuito_guante (saved by Fritzing 1.0.5)
perfboards: 1

parts:
  R1 = Basic Flex Resistor
  R2 = Basic Flex Resistor  # not connected
  Componente1 = Analog Digital MUX Breakout
  Componente2 = ADS1115
  A1 = Esp32-c3 super mini
  U1 = POT [knob_status=50% power=0.5W package=pot_mammoth]
  U2 = POT [knob_status=50% power=0.5W package=pot_mammoth]
  U3 = POT [knob_status=50% power=0.5W package=pot_mammoth]
  U4 = POT [knob_status=50% power=0.5W package=pot_mammoth]
  U5 = POT [knob_status=50% power=0.5W package=pot_mammoth]
  R3 = Basic Flex Resistor
  R4 = Basic Flex Resistor
  R5 = Basic Flex Resistor
  R6 = Resistor [tolerance=±5% resistance=220 package="0805 [SMD]"]  # not connected
  R7 = Resistor [tolerance=±5% resistance=220 package="0805 [SMD]"]  # not connected
  R8 = Resistor [tolerance=±5% resistance=220 package="0805 [SMD]"]
  R9 = Resistor [tolerance=±5% resistance=220 package="0805 [SMD]"]
  R10 = Resistor [tolerance=±5% resistance=220 package="0805 [SMD]"]
  U6 = POT [knob_status=50% power=0.5W package=pot_mammoth]
  R11 = Basic Flex Resistor
  R12 = Basic Flex Resistor
  R13 = Resistor [tolerance=±5% resistance=220 package="0805 [SMD]"]
  R14 = Resistor [tolerance=±5% resistance=220 package="0805 [SMD]"]  # not connected

nets:
  N1: R1.Pin_2, R5.Pin_2
  N2: Componente1.C1, U6.A
  N3: Componente1.C2, U5.A
  N4: Componente1.C3, U2.A
  N5: Componente1.C4, U3.A
  N6: Componente1.C5, U1.A
  N7: Componente1.C6, U4.A
  N8: Componente1.C8, R11.Pin_1
  N9: Componente1.C12, R10.Pin_0
  N10: Componente1.C13, R3.pin_1, R9.Pin_0
  N11: Componente1.VCC, U2.E, U4.E
  N12: Componente1.EN, Componente2.GND, A1.Pin_15
  N13: Componente1.S0, A1.Pin_6
  N14: Componente1.S1, A1.Pin_11
  N15: Componente1.S2, A1.Pin_12
  N16: Componente1.S3, A1.Pin_13
  N17: Componente1.SIG, Componente2.A0
  N18: Componente2.VDD, A1.Pin_14
  N19: Componente2.SCL, A1.Pin_5
  N20: Componente2.SDA, A1.Pin_4
  N21: R4.pin_1, R8.Pin_0
  N22: R12.Pin_1, R13.Pin_0

notes:
  Circuito guante
  D1
  D2
  D3
  D4
  D5
  M1
  M2
  P0
  P1
  P2
  P3
  P4
  P5
  Ads1115
  CD74hc4067
  ESP32-S3 mini
  POTENCIOMETROS
  SENSORES FLEX

custom parts:
  ADS1115: ADC ADS1115
  Esp32-c3 super mini: ESP32-C3 Development Board ESP32 SuperMini Development Board ESP32 Development Board WiFi Bluetooth.
